# Fritzing sketch fritzing_sketch2 (saved by Fritzing 0.9.0b)
circuit board: 10cm x 5.2cm
breadboards: 1

parts:
  VCC1 = Battery block 9V
  D1 = Diode [package=diode-1n4001]
  R10 = Resistor [tolerance=±5% resistance=33k package=THT]
  T3_BC557C = PNP-Transistor [package="TO92 [THT]"]
  R7 = Resistor [tolerance=±5% resistance=3.3k package=THT]
  U1 = Voltage Regulator - 5V [package="TO220 [THT]"]
  C5 = Ceramic Capacitor [capacitance=100nF package="100 mil [THT, multilayer]"]
  C9 = Electrolytic Capacitor [capacitance=10nF package="100 mil [THT, electrolytic]"]
  C6 = Ceramic Capacitor [capacitance=100nF package="100 mil [THT, multilayer]"]
  T1_BC547 = NPN-Transistor [package="TO92 [THT]"]
  LED1 = LED - 5mm [color="Red (633nm)" package="5 mm [THT]"]
  T2_BC547 = NPN-Transistor [package="TO92 [THT]"]
  R15 = Resistor [tolerance=±5% resistance=27k package=THT]
  C1 = Ceramic Capacitor [capacitance=1nF package="100 mil [THT, multilayer]"]
  R8 = Resistor [tolerance=±5% resistance=27k package=THT]
  C2 = Ceramic Capacitor [capacitance=10nF package="100 mil [THT, multilayer]"]
  R9 = Resistor [tolerance=±5% resistance=100k package=THT]
  C11 = Ceramic Capacitor [capacitance=100nF package="100 mil [THT, multilayer]"]
  C3 = Ceramic Capacitor [capacitance=100nF package="100 mil [THT, multilayer]"]
  R13 = Resistor [tolerance=±5% resistance=10k package=THT]
  C10 = Electrolytic Capacitor [capacitance=10µF package="100 mil [THT, electrolytic]"]
  R1 = Resistor [tolerance=±5% resistance=680 package=THT]
  R3 = Resistor [tolerance=±5% resistance=680 package=THT]
  R5 = Resistor [tolerance=±5% resistance=680 package=THT]
  R2 = Resistor [tolerance=±5% resistance=470k package=THT]
  R4 = Resistor [tolerance=±5% resistance=470k package=THT]
  R6 = Resistor [tolerance=±5% resistance=470k package=THT]
  JP2 = Header 5x2 [package=2x5-ra]
  LCD1 = LCD screen
  XTAL1 = Crystal [frequency="8 MHz" package=THT]
  C11_2 = Ceramic Capacitor [capacitance=22pF package="100 mil [THT, multilayer]"]
  C12 = Ceramic Capacitor [capacitance=22pF package="100 mil [THT, multilayer]"]
  JP3 = Header 1 [package=1x01_offset]
  S1 = Round Pushbutton
  JP5 = Header 1 [package=1x01_offset]
  Q1 = TRANSISTOR_NPN [package=to-92-ammo]
  R12 = Resistor [tolerance=±5% resistance=3.3k package=THT]
  R11 = Resistor [tolerance=±5% resistance=10k package=THT]
  R16 = Resistor [tolerance=±5% resistance=2.2k package=THT]
  JP4 = Header 1 [package=1x01_offset]
  JP6 = Header 1 [package=1x01_offset]
  JP1 = Header 5x2 [package=2x5-ra]
  IC1 = MICROCONTROLLER [package=dil28-3]

nets:
  GND: VCC1.-, U1.GND, C5.0, C9.-, C6.0, T1_BC547.E, T2_BC547.E, C1.1, C2.0, R9.Pin_0, C11.0, C3.0, C10.-, JP2.8, C11_2.0, C12.0, Q1.E, R12.Pin_0, JP1.4, JP1.6, JP1.8, JP1.10, IC1.GND, IC1.AGND
  N1: VCC1.+, D1.A
  N2: D1.C, R10.Pin_0, T3_BC557C.E
  N3: R10.Pin_1, T3_BC557C.B, R7.Pin_1
  N4: T3_BC557C.C, U1.input_voltage, C5.1, C9.+, R11.Pin_1
  N5: R7.Pin_0, LED1.anode, S1.leg0
  N6: U1.output_voltage, C6.1, R15.Pin_1, C1.0, C3.1, R13.Pin_0, C10.+, JP2.10, R16.Pin_1, JP1.2, IC1.VCC, IC1.AVCC
  N7: T1_BC547.B, R8.Pin_0, C2.1, R9.Pin_1
  N8: T1_BC547.C, LED1.cathode
  N9: T2_BC547.B, S1.leg1
  N10: T2_BC547.C, R15.Pin_0, IC1.PD7(AIN1)
  N11: R8.Pin_1, IC1.PD6(AIN0)
  N12: C11.1, IC1.AREF
  N13: R13.Pin_1, JP1.5, IC1.PC6(_RESET)
  N14: R1.Pin_0, IC1.PB0(ICP)
  N15: R1.Pin_1, R2.Pin_1, JP3.1, IC1.PC0(ADC0)
  N16: R3.Pin_0, IC1.PB2(SS_OC1B)
  N17: R3.Pin_1, R4.Pin_1, JP4.1, IC1.PC1(ADC1)
  N18: R5.Pin_0, JP1.9, IC1.PB4(MISO)
  N19: R5.Pin_1, R6.Pin_1, JP5.1, IC1.PC2(ADC2)
  N20: R2.Pin_0, IC1.PB1(OC1A)
  N21: R4.Pin_0, JP1.1, IC1.PB3(MOSI_OC2)
  N22: R6.Pin_0, JP1.7, IC1.PB5(SCK)
  N23: JP2.1, LCD1.DB7, IC1.PD3(INT1)
  N24: JP2.2, LCD1.RS, IC1.PD4(XCK_T0)
  N25: JP2.3, LCD1.DB6, IC1.PD2(INT0)
  N26: JP2.5, LCD1.DB5, IC1.PD1(TXD)
  N27: JP2.7, LCD1.DB4, IC1.PD0(RXD)
  N28: JP2.9, LCD1.E, IC1.PD5(T1)
  N29: XTAL1.pin_0, C11_2.1, IC1.PB6(XTAL1_TOSC1)
  N30: XTAL1.pin_1, C12.1, IC1.PB7(XTAL2_TOSC2)
  N31: Q1.B, R16.Pin_0, IC1.PC4(ADC4_SDA)
  N32: R12.Pin_1, R11.Pin_0, IC1.PC5(ADC5_SCL)
  N33: JP6.1, IC1.PC3(ADC3)
